// Logisim project 16-bit_CPU_70%.circ as structural Verilog
module _8x16_bit_Register_File (
  input  [15:0] Data_In,
  input  [2:0] Read_Addr_1,
  input  Write_Enable,
  input  [2:0] Write_Addr,
  input  [2:0] Read_Addr_2,
  input  Clock,
  output [15:0] Read_1_Data,
  output [15:0] Read_2_Data
);

  wire demultiplexer_1_out0, demultiplexer_1_out1, demultiplexer_1_out2, demultiplexer_1_out3,
       demultiplexer_1_out4, demultiplexer_1_out5, demultiplexer_1_out6, demultiplexer_1_out7;
  wire [15:0] register_1_q, register_2_q, register_3_q, register_4_q, register_5_q, register_6_q,
       register_7_q, register_8_q;

  Demultiplexer #(.select(3), .enable("false")) demultiplexer_1 (
    .out0(demultiplexer_1_out0), .out1(demultiplexer_1_out1), .out2(demultiplexer_1_out2),
    .out3(demultiplexer_1_out3), .out4(demultiplexer_1_out4), .out5(demultiplexer_1_out5),
    .out6(demultiplexer_1_out6), .out7(demultiplexer_1_out7), .in(Write_Enable), .sel(Write_Addr));
  Register #(.width(16)) register_1 (
    .D(Data_In), .en(demultiplexer_1_out0), .Q(register_1_q), .clk(Clock));  // open: clr
  Register #(.width(16)) register_2 (
    .D(Data_In), .en(demultiplexer_1_out1), .Q(register_2_q), .clk(Clock));  // open: clr
  Register #(.width(16)) register_3 (
    .D(Data_In), .en(demultiplexer_1_out2), .Q(register_3_q), .clk(Clock));  // open: clr
  Register #(.width(16)) register_4 (
    .D(Data_In), .en(demultiplexer_1_out3), .Q(register_4_q), .clk(Clock));  // open: clr
  Register #(.width(16)) register_5 (
    .D(Data_In), .en(demultiplexer_1_out4), .Q(register_5_q), .clk(Clock));  // open: clr
  Register #(.width(16)) register_6 (
    .D(Data_In), .en(demultiplexer_1_out5), .Q(register_6_q), .clk(Clock));  // open: clr
  Register #(.width(16)) register_7 (
    .D(Data_In), .en(demultiplexer_1_out6), .Q(register_7_q), .clk(Clock));  // open: clr
  Register #(.width(16)) register_8 (
    .D(Data_In), .en(demultiplexer_1_out7), .Q(register_8_q), .clk(Clock));  // open: clr
  Multiplexer #(.select(3), .width(16), .enable("false")) multiplexer_1 (
    .in0(register_1_q), .in1(register_2_q), .in2(register_3_q), .in3(register_4_q), .in4(register_5_q),
    .in5(register_6_q), .in6(register_7_q), .in7(register_8_q), .out(Read_1_Data), .sel(Read_Addr_1));
  Multiplexer #(.select(3), .width(16), .enable("false")) multiplexer_2 (
    .in0(register_1_q), .in1(register_2_q), .in2(register_3_q), .in3(register_4_q), .in4(register_5_q),
    .in5(register_6_q), .in6(register_7_q), .in7(register_8_q), .out(Read_2_Data), .sel(Read_Addr_2));

  // Notes on the sheet:
  //   8x16-bit Register File
endmodule

module _16_bit_ALU (
  input  [15:0] A,
  input  [15:0] B,
  input  [1:0] ALU_Op,
  output [15:0] ALU_Out
);

  wire and_1_out;
  wire [15:0] adder_1_out, and_2_out, multiplexer_1_out, not_1_out, or_1_out;

  Multiplexer #(.width(16), .enable("false")) multiplexer_1 (
    .in0(B), .in1(not_1_out), .out(multiplexer_1_out), .sel(and_1_out));
  assign not_1_out = ~B;  // NOT_Gate not_1, 16 bits wide
  and and_1 (and_1_out, ALU_Op[0], ALU_Op[1]);
  Adder #(.width(16)) adder_1 (.a(A), .b(multiplexer_1_out), .out(adder_1_out), .cin(and_1_out));  // open: cout
  assign and_2_out = multiplexer_1_out & A;  // AND_Gate and_2, 16 bits wide
  assign or_1_out = multiplexer_1_out | A;  // OR_Gate or_1, 16 bits wide
  Multiplexer #(.select(2), .width(16), .enable("false")) multiplexer_2 (
    .in0(adder_1_out), .in1(and_2_out), .in2(or_1_out), .in3(adder_1_out), .out(ALU_Out), .sel(ALU_Op));

  // Notes on the sheet:
  //   sub not B
  //   sub cin
  //   sub
  //   16 Bit ALU
  //   00 = ADD
  //   01 = AND
  //   10 = OR
  //   11 = SUB
endmodule

module Control_Logic (
  input  [4:0] Control_Logic_OP,
  output I_R,
  output SW,
  output LW,
  output [1:0] OP
);


  assign I_R = Control_Logic_OP[4];
  assign LW = Control_Logic_OP[2];
  assign OP = Control_Logic_OP[1:0];
  assign SW = Control_Logic_OP[3];
endmodule

module _16_bit_CPU (
  input  clock
);

  wire Control_Logic_i_r, Control_Logic_lw, Control_Logic_sw, not_1_out;
  wire [1:0] Control_Logic_op;
  wire [2:0] multiplexer_1_out;
  wire [15:0] _16_bit_ALU_p2, _16_bit_ALU_p4, _16_bit_Reg_read_1_data, _16_bit_Reg_read_2_data, adder_1_out,
       multiplexer_2_out, PC_q, ram_2_data;
  wire [26:0] ram_1_data;

  Register #(.width(16)) PC (.D(adder_1_out), .en(1'b1), .Q(PC_q), .clk(clock));  // open: clr
  Adder #(.width(16)) adder_1 (.a(16'h1), .b(PC_q), .out(adder_1_out));  // open: cin, cout
  RAM #(.addrWidth(16), .dataWidth(27)) ram_1 (.addr(PC_q), .data(ram_1_data), .clk(clock));  // open: sel, ld, clr
  not not_1 (not_1_out, Control_Logic_sw);
  Control_Logic Control_Logic (
    .Control_Logic_OP(ram_1_data[26:22]), .I_R(Control_Logic_i_r), .SW(Control_Logic_sw),
    .LW(Control_Logic_lw), .OP(Control_Logic_op));
  Multiplexer #(.width(3), .enable("false")) multiplexer_1 (
    .in0(ram_1_data[15:13]), .in1(ram_1_data[21:19]), .out(multiplexer_1_out), .sel(Control_Logic_sw));
  _8x16_bit_Register_File _16_bit_Reg (
    .Data_In(multiplexer_2_out), .Write_Enable(not_1_out), .Clock(clock), .Write_Addr(ram_1_data[21:19]),
    .Read_Addr_1(ram_1_data[18:16]), .Read_Addr_2(multiplexer_1_out), .Read_1_Data(_16_bit_Reg_read_1_data),
    .Read_2_Data(_16_bit_Reg_read_2_data));
  Multiplexer #(.width(16), .enable("false")) multiplexer_2 (
    .in0(_16_bit_ALU_p4), .in1(ram_2_data), .out(multiplexer_2_out), .sel(Control_Logic_lw));
  // _16_bit_ALU _16_bit_ALU: pin names not known; wires that end beside it: _16_bit_Reg_read_1_data, _16_bit_ALU_p2, Control_Logic_op, _16_bit_ALU_p4
  Multiplexer #(.width(16), .enable("false")) multiplexer_3 (
    .in0(_16_bit_Reg_read_2_data), .in1(ram_1_data[15:0]), .out(_16_bit_ALU_p2), .sel(Control_Logic_i_r));
  RAM #(.addrWidth(16), .dataWidth(16), .bus("separate")) ram_2 (
    .addr(_16_bit_ALU_p4), .din(_16_bit_Reg_read_2_data), .data(ram_2_data), .str(Control_Logic_sw),
    .clk(clock));  // open: sel, ld, clr

  // Notes on the sheet:
  //   Instruction Memory
  //   src2
  //   op
  //   WE
  //   imm data
  //   src1
  //   imm select
  //   dest
  //   ALU op
  //   SW
  //   LW
  //   Data Memory
endmodule
