// Logisim project CSC_270_Final_Project.circ as structural Verilog
module _8x16_bit_Register_File (
  input  [15:0] Data_In,
  input  [2:0] Read_Addr_1,
  input  Write_Enable,
  input  [2:0] Write_Addr,
  input  [2:0] Read_Addr_2,
  input  Clock,
  output [15:0] Read_1_Data,
  output [15:0] Read_2_Data
);

  wire demultiplexer_1_out0, demultiplexer_1_out1, demultiplexer_1_out2, demultiplexer_1_out3,
       demultiplexer_1_out4, demultiplexer_1_out5, demultiplexer_1_out6, demultiplexer_1_out7;
  wire [15:0] register_1_q, register_2_q, register_3_q, register_4_q, register_5_q, register_6_q,
       register_7_q, register_8_q;

  Demultiplexer #(.select(3), .enable("false")) demultiplexer_1 (
    .out0(demultiplexer_1_out0), .out1(demultiplexer_1_out1), .out2(demultiplexer_1_out2),
    .out3(demultiplexer_1_out3), .out4(demultiplexer_1_out4), .out5(demultiplexer_1_out5),
    .out6(demultiplexer_1_out6), .out7(demultiplexer_1_out7), .in(Write_Enable), .sel(Write_Addr));
  Register #(.width(16)) register_1 (
    .D(Data_In), .en(demultiplexer_1_out0), .Q(register_1_q), .clk(Clock));  // open: clr
  Register #(.width(16)) register_2 (
    .D(Data_In), .en(demultiplexer_1_out1), .Q(register_2_q), .clk(Clock));  // open: clr
  Register #(.width(16)) register_3 (
    .D(Data_In), .en(demultiplexer_1_out2), .Q(register_3_q), .clk(Clock));  // open: clr
  Register #(.width(16)) register_4 (
    .D(Data_In), .en(demultiplexer_1_out3), .Q(register_4_q), .clk(Clock));  // open: clr
  Register #(.width(16)) register_5 (
    .D(Data_In), .en(demultiplexer_1_out4), .Q(register_5_q), .clk(Clock));  // open: clr
  Register #(.width(16)) register_6 (
    .D(Data_In), .en(demultiplexer_1_out5), .Q(register_6_q), .clk(Clock));  // open: clr
  Register #(.width(16)) register_7 (
    .D(Data_In), .en(demultiplexer_1_out6), .Q(register_7_q), .clk(Clock));  // open: clr
  Register #(.width(16)) register_8 (
    .D(Data_In), .en(demultiplexer_1_out7), .Q(register_8_q), .clk(Clock));  // open: clr
  Multiplexer #(.select(3), .width(16), .enable("false")) multiplexer_1 (
    .in0(register_1_q), .in1(register_2_q), .in2(register_3_q), .in3(register_4_q), .in4(register_5_q),
    .in5(register_6_q), .in6(register_7_q), .in7(register_8_q), .out(Read_1_Data), .sel(Read_Addr_1));
  Multiplexer #(.select(3), .width(16), .enable("false")) multiplexer_2 (
    .in0(register_1_q), .in1(register_2_q), .in2(register_3_q), .in3(register_4_q), .in4(register_5_q),
    .in5(register_6_q), .in6(register_7_q), .in7(register_8_q), .out(Read_2_Data), .sel(Read_Addr_2));

  // Notes on the sheet:
  //   8x16-bit Register File
endmodule

module _16_bit_ALU (
  input  [15:0] A,
  input  [15:0] B,
  input  [1:0] ALU_Op,
  output [15:0] ALU_Out
);

  wire and_1_out;
  wire [15:0] adder_1_out, and_2_out, multiplexer_1_out, not_1_out, or_1_out;

  Multiplexer #(.width(16), .enable("false")) multiplexer_1 (
    .in0(B), .in1(not_1_out), .out(multiplexer_1_out), .sel(and_1_out));
  assign not_1_out = ~B;  // NOT_Gate not_1, 16 bits wide
  and and_1 (and_1_out, ALU_Op[0], ALU_Op[1]);
  Adder #(.width(16)) adder_1 (.a(A), .b(multiplexer_1_out), .out(adder_1_out), .cin(and_1_out));  // open: cout
  assign and_2_out = multiplexer_1_out & A;  // AND_Gate and_2, 16 bits wide
  assign or_1_out = multiplexer_1_out | A;  // OR_Gate or_1, 16 bits wide
  Multiplexer #(.select(2), .width(16), .enable("false")) multiplexer_2 (
    .in0(adder_1_out), .in1(and_2_out), .in2(or_1_out), .in3(adder_1_out), .out(ALU_Out), .sel(ALU_Op));

  // Notes on the sheet:
  //   sub not B
  //   sub cin
  //   sub
  //   16 Bit ALU
  //   00 = ADD
  //   01 = AND
  //   10 = OR
  //   11 = SUB
endmodule

module Control_Logic (
  input  [4:0] Control_Logic_OP,
  output I_R,
  output SW,
  output LW,
  output [1:0] OP
);


  assign I_R = Control_Logic_OP[4];
  assign LW = Control_Logic_OP[2];
  assign OP = Control_Logic_OP[1:0];
  assign SW = Control_Logic_OP[3];
endmodule

module _16_bit_CPU (
  input  clock
);

  wire Control_Logic_i_r, Control_Logic_lw, Control_Logic_sw, not_1_out;
  wire [1:0] Control_Logic_op;
  wire [2:0] multiplexer_1_out;
  wire [15:0] _16_bit_ALU_p2, _16_bit_ALU_p4, _16_bit_Reg_read_1_data, _16_bit_Reg_read_2_data, adder_1_out,
       multiplexer_2_out, PC_q, ram_2_data;
  wire [26:0] ram_1_data;

  Register #(.width(16)) PC (.D(adder_1_out), .en(1'b1), .Q(PC_q), .clk(clock));  // open: clr
  Adder #(.width(16)) adder_1 (.a(16'h1), .b(PC_q), .out(adder_1_out));  // open: cin, cout
  RAM #(.addrWidth(16), .dataWidth(27)) ram_1 (.addr(PC_q), .data(ram_1_data), .clk(clock));  // open: sel, ld, clr
  not not_1 (not_1_out, Control_Logic_sw);
  Control_Logic Control_Logic (
    .Control_Logic_OP(ram_1_data[26:22]), .I_R(Control_Logic_i_r), .SW(Control_Logic_sw),
    .LW(Control_Logic_lw), .OP(Control_Logic_op));
  Multiplexer #(.width(3), .enable("false")) multiplexer_1 (
    .in0(ram_1_data[15:13]), .in1(ram_1_data[21:19]), .out(multiplexer_1_out), .sel(Control_Logic_sw));
  _8x16_bit_Register_File _16_bit_Reg (
    .Data_In(multiplexer_2_out), .Write_Enable(not_1_out), .Clock(clock), .Write_Addr(ram_1_data[21:19]),
    .Read_Addr_1(ram_1_data[18:16]), .Read_Addr_2(multiplexer_1_out), .Read_1_Data(_16_bit_Reg_read_1_data),
    .Read_2_Data(_16_bit_Reg_read_2_data));
  Multiplexer #(.width(16), .enable("false")) multiplexer_2 (
    .in0(_16_bit_ALU_p4), .in1(ram_2_data), .out(multiplexer_2_out), .sel(Control_Logic_lw));
  // _16_bit_ALU _16_bit_ALU: pin names not known; wires that end beside it: _16_bit_Reg_read_1_data, _16_bit_ALU_p2, Control_Logic_op, _16_bit_ALU_p4
  Multiplexer #(.width(16), .enable("false")) multiplexer_3 (
    .in0(_16_bit_Reg_read_2_data), .in1(ram_1_data[15:0]), .out(_16_bit_ALU_p2), .sel(Control_Logic_i_r));
  RAM #(.addrWidth(16), .dataWidth(16), .bus("separate")) ram_2 (
    .addr(_16_bit_ALU_p4), .din(_16_bit_Reg_read_2_data), .data(ram_2_data), .str(Control_Logic_sw),
    .clk(clock));  // open: sel, ld, clr

  // Notes on the sheet:
  //   Instruction Memory
  //   src2
  //   op
  //   WE
  //   imm data
  //   src1
  //   imm select
  //   dest
  //   ALU op
  //   SW
  //   LW
  //   Data Memory
endmodule

module Full_ALU (
  input  [15:0] A,
  input  [15:0] B,
  input  [2:0] ALU_Control,
  output Zero,
  output [15:0] ALU_Out
);

  wire and_1_out, or_2_out;
  wire [15:0] adder_1_out, and_2_out, multiplexer_1_out, not_1_out, or_1_out;

  Multiplexer #(.width(16), .enable("false")) multiplexer_1 (
    .in0(B), .in1(not_1_out), .out(multiplexer_1_out), .sel(and_1_out));
  assign not_1_out = ~B;  // NOT_Gate not_1, 16 bits wide
  and and_1 (and_1_out, ALU_Control[1], ALU_Control[2]);
  assign and_2_out = A & multiplexer_1_out;  // AND_Gate and_2, 16 bits wide
  assign or_1_out = A | multiplexer_1_out;  // OR_Gate or_1, 16 bits wide
  Adder #(.width(16)) adder_1 (.a(A), .b(multiplexer_1_out), .out(adder_1_out), .cin(and_1_out));  // open: cout
  Multiplexer #(.select(3), .width(16), .enable("false")) multiplexer_2 (
    .in0(and_2_out), .in1(or_1_out), .in2(adder_1_out), .in6(adder_1_out), .out(ALU_Out), .sel(ALU_Control));  // open: in3, in4, in5, in7
  not not_2 (Zero, or_2_out);
  or or_2 (or_2_out, ALU_Out[0], ALU_Out[1], ALU_Out[2], ALU_Out[3], ALU_Out[4], ALU_Out[5], ALU_Out[6], ALU_Out[7], ALU_Out[8], ALU_Out[9], ALU_Out[10], ALU_Out[11], ALU_Out[12], ALU_Out[13], ALU_Out[14], ALU_Out[15]);

  // Notes on the sheet:
  //   000 - AND
  //   001 - OR
  //   010 - ADD
  //   110 - SUB
  //   sub not B
  //   sub cin
  //   sub
endmodule

module ALU_Control (
  input  [5:0] Function_code,
  input  [1:0] ALU_OP,
  output [2:0] Operation
);

  wire and_1_out, not_1_out, not_2_out, or_1_out;

  or or_1 (or_1_out, Function_code[3], Function_code[0]);
  and and_1 (and_1_out, ALU_OP[1], Function_code[1]);
  and and_2 (Operation[0], ALU_OP[1], or_1_out);
  or or_2 (Operation[2], ALU_OP[0], and_1_out);
  not not_1 (not_1_out, ALU_OP[1]);
  or or_3 (Operation[1], not_1_out, not_2_out);
  not not_2 (not_2_out, Function_code[2]);
endmodule

module Control_Logic_w__branch (
  input  [5:0] in_1,
  output RegDest,
  output ALUSrc,
  output MemToReg,
  output RegWrite,
  output MemRead,
  output MemWrite,
  output Branch,
  output [1:0] ALUOP
);

  wire and_5_out;

  and and_1 (ALUOP[1], ~in_1[5], ~in_1[4], ~in_1[3], ~in_1[2], ~in_1[1], ~in_1[0]);  // AND_Gate
  and and_2 (MemRead, in_1[5], ~in_1[4], ~in_1[3], ~in_1[2], in_1[1], in_1[0]);  // AND_Gate
  and and_3 (MemWrite, in_1[5], ~in_1[4], in_1[3], ~in_1[2], in_1[1], in_1[0]);  // AND_Gate
  and and_4 (ALUOP[0], ~in_1[5], ~in_1[4], ~in_1[3], in_1[2], ~in_1[1], ~in_1[0]);  // AND_Gate
  and and_5 (and_5_out, ~in_1[5], ~in_1[4], in_1[3], ~in_1[2], ~in_1[1], ~in_1[0]);  // AND_Gate
  or or_1 (ALUSrc, MemRead, and_5_out, MemWrite);
  or or_2 (RegWrite, ALUOP[1], and_5_out, MemRead);

  assign Branch = ALUOP[0];
  assign MemToReg = MemRead;
  assign RegDest = ALUOP[1];

  // Notes on the sheet:
  //   R-format
  //   000000
  //   lw
  //   100011
  //   sw
  //   101011
  //   beq
  //   000100
  //   addi
  //   001000
endmodule

module _16_bit_CPU_w__branch (
  input  clock
);

  wire and_1_out, control_logic_w_branch_1_alusrc, control_logic_w_branch_1_branch,
       control_logic_w_branch_1_memread, control_logic_w_branch_1_memtoreg,
       control_logic_w_branch_1_memwrite, control_logic_w_branch_1_regdest,
       control_logic_w_branch_1_regwrite, full_alu_1_zero;
  wire [1:0] control_logic_w_branch_1_aluop;
  wire [2:0] ALUControl_operation, multiplexer_1_out;
  wire [15:0] _16_bit_Reg_read_1_data, _16_bit_Reg_read_2_data, adder_1_out, adder_2_out, full_alu_1_alu_out,
       multiplexer_2_out, multiplexer_3_out, multiplexer_4_out, PC_q, ram_2_data;
  wire [27:0] ram_1_data;

  Register #(.width(16)) PC (.D(multiplexer_3_out), .Q(PC_q), .clk(clock));  // open: en, clr
  Adder #(.width(16)) adder_1 (.a(16'h1), .b(PC_q), .out(adder_1_out));  // open: cin, cout
  RAM #(.addrWidth(16), .dataWidth(28)) ram_1 (.addr(PC_q), .data(ram_1_data), .clk(clock));  // open: sel, ld, clr
  Control_Logic_w__branch control_logic_w_branch_1 (
    .in_1(ram_1_data[27:22]), .RegDest(control_logic_w_branch_1_regdest),
    .ALUSrc(control_logic_w_branch_1_alusrc), .MemToReg(control_logic_w_branch_1_memtoreg),
    .RegWrite(control_logic_w_branch_1_regwrite), .MemRead(control_logic_w_branch_1_memread),
    .MemWrite(control_logic_w_branch_1_memwrite), .Branch(control_logic_w_branch_1_branch),
    .ALUOP(control_logic_w_branch_1_aluop));
  Multiplexer #(.width(3), .enable("false")) multiplexer_1 (
    .in0(ram_1_data[21:19]), .in1(ram_1_data[15:13]), .out(multiplexer_1_out),
    .sel(control_logic_w_branch_1_regdest));
  _8x16_bit_Register_File _16_bit_Reg (
    .Data_In(multiplexer_4_out), .Write_Enable(control_logic_w_branch_1_regwrite), .Clock(clock),
    .Write_Addr(ram_1_data[21:19]), .Read_Addr_1(ram_1_data[18:16]), .Read_Addr_2(multiplexer_1_out),
    .Read_1_Data(_16_bit_Reg_read_1_data), .Read_2_Data(_16_bit_Reg_read_2_data));
  Adder #(.width(16)) adder_2 (.a(adder_1_out), .b(ram_1_data[15:0]), .out(adder_2_out));  // open: cin, cout
  Multiplexer #(.width(16), .enable("false")) multiplexer_2 (
    .in0(_16_bit_Reg_read_2_data), .in1(ram_1_data[15:0]), .out(multiplexer_2_out),
    .sel(control_logic_w_branch_1_alusrc));
  and and_1 (and_1_out, full_alu_1_zero, control_logic_w_branch_1_branch);
  Full_ALU full_alu_1 (
    .A(_16_bit_Reg_read_1_data), .B(multiplexer_2_out), .ALU_Control(ALUControl_operation),
    .Zero(full_alu_1_zero), .ALU_Out(full_alu_1_alu_out));
  ALU_Control ALUControl (
    .Function_code(ram_1_data[5:0]), .ALU_OP(control_logic_w_branch_1_aluop), .Operation(ALUControl_operation));
  Multiplexer #(.width(16), .enable("false")) multiplexer_3 (
    .in0(adder_1_out), .in1(adder_2_out), .out(multiplexer_3_out), .sel(and_1_out));
  Multiplexer #(.width(16), .enable("false")) multiplexer_4 (
    .in0(full_alu_1_alu_out), .in1(ram_2_data), .out(multiplexer_4_out),
    .sel(control_logic_w_branch_1_memtoreg));
  RAM #(.addrWidth(16), .dataWidth(16), .bus("separate")) ram_2 (
    .addr(full_alu_1_alu_out), .din(_16_bit_Reg_read_2_data), .data(ram_2_data),
    .str(control_logic_w_branch_1_memwrite), .clk(clock), .ld(control_logic_w_branch_1_memread));  // open: sel, clr

  // Notes on the sheet:
  //   Instruction Memory
  //   op
  //   src2
  //   WE
  //   Control Logic
  //   dest
  //   src1
  //   immed data
  //   RegDest
  //   ALUOP
  //   Function code
  //   ALUSrc
  //   Zero
  //   Full ALU
  //   Branch
  //   MemToReg
  //   MemWrite
  //   MemRead
  //   Data Memory
endmodule

module Control_Logic_w__b__j (
  input  [5:0] in_1,
  output RegDest,
  output ALUSrc,
  output MemToReg,
  output RegWrite,
  output MemRead,
  output MemWrite,
  output Branch,
  output [1:0] ALUOP,
  output Jump
);

  wire and_5_out;

  and and_1 (ALUOP[1], ~in_1[5], ~in_1[4], ~in_1[3], ~in_1[2], ~in_1[1], ~in_1[0]);  // AND_Gate
  and and_2 (MemRead, in_1[5], ~in_1[4], ~in_1[3], ~in_1[2], in_1[1], in_1[0]);  // AND_Gate
  and and_3 (MemWrite, in_1[5], ~in_1[4], in_1[3], ~in_1[2], in_1[1], in_1[0]);  // AND_Gate
  and and_4 (ALUOP[0], ~in_1[5], ~in_1[4], ~in_1[3], in_1[2], ~in_1[1], ~in_1[0]);  // AND_Gate
  and and_5 (and_5_out, ~in_1[5], ~in_1[4], in_1[3], ~in_1[2], ~in_1[1], ~in_1[0]);  // AND_Gate
  and and_6 (Jump, ~in_1[5], ~in_1[4], ~in_1[3], ~in_1[2], in_1[1], ~in_1[0]);  // AND_Gate
  or or_1 (ALUSrc, MemRead, and_5_out, MemWrite);
  or or_2 (RegWrite, ALUOP[1], and_5_out, MemRead);

  assign Branch = ALUOP[0];
  assign MemToReg = MemRead;
  assign RegDest = ALUOP[1];

  // Notes on the sheet:
  //   R-format
  //   000000
  //   lw
  //   100011
  //   sw
  //   101011
  //   beq
  //   000100
  //   addi
  //   001000
  //   jump
  //   000010
endmodule

module _16_bit_CPU_w__b__j (
  input  clock
);

  wire and_1_out, control_logic_w_b_j_1_alusrc, control_logic_w_b_j_1_branch, control_logic_w_b_j_1_jump,
       control_logic_w_b_j_1_memread, control_logic_w_b_j_1_memtoreg, control_logic_w_b_j_1_memwrite,
       control_logic_w_b_j_1_regdest, control_logic_w_b_j_1_regwrite, full_alu_1_zero;
  wire [1:0] control_logic_w_b_j_1_aluop;
  wire [2:0] ALUControl_operation, multiplexer_1_out;
  wire [15:0] _16_bit_Reg_read_1_data, _16_bit_Reg_read_2_data, adder_1_out, adder_2_out, full_alu_1_alu_out,
       multiplexer_2_out, multiplexer_3_out, multiplexer_4_out, multiplexer_5_out, PC_q, ram_2_data;
  wire [27:0] ram_1_data;

  Register #(.width(16)) PC (.D(multiplexer_4_out), .Q(PC_q), .clk(clock));  // open: en, clr
  Adder #(.width(16)) adder_1 (.a(16'h1), .b(PC_q), .out(adder_1_out));  // open: cin, cout
  RAM #(.addrWidth(16), .dataWidth(28)) ram_1 (.addr(PC_q), .data(ram_1_data), .clk(clock));  // open: sel, ld, clr
  Control_Logic_w__b__j control_logic_w_b_j_1 (
    .in_1(ram_1_data[27:22]), .RegDest(control_logic_w_b_j_1_regdest), .ALUSrc(control_logic_w_b_j_1_alusrc),
    .MemToReg(control_logic_w_b_j_1_memtoreg), .RegWrite(control_logic_w_b_j_1_regwrite),
    .MemRead(control_logic_w_b_j_1_memread), .MemWrite(control_logic_w_b_j_1_memwrite),
    .Branch(control_logic_w_b_j_1_branch), .ALUOP(control_logic_w_b_j_1_aluop),
    .Jump(control_logic_w_b_j_1_jump));
  Multiplexer #(.width(3), .enable("false")) multiplexer_1 (
    .in0(ram_1_data[21:19]), .in1(ram_1_data[15:13]), .out(multiplexer_1_out),
    .sel(control_logic_w_b_j_1_regdest));
  _8x16_bit_Register_File _16_bit_Reg (
    .Data_In(multiplexer_5_out), .Write_Enable(control_logic_w_b_j_1_regwrite), .Clock(clock),
    .Write_Addr(ram_1_data[21:19]), .Read_Addr_1(ram_1_data[18:16]), .Read_Addr_2(multiplexer_1_out),
    .Read_1_Data(_16_bit_Reg_read_1_data), .Read_2_Data(_16_bit_Reg_read_2_data));
  Adder #(.width(16)) adder_2 (.a(adder_1_out), .b(ram_1_data[15:0]), .out(adder_2_out));  // open: cin, cout
  Multiplexer #(.width(16), .enable("false")) multiplexer_2 (
    .in0(_16_bit_Reg_read_2_data), .in1(ram_1_data[15:0]), .out(multiplexer_2_out),
    .sel(control_logic_w_b_j_1_alusrc));
  and and_1 (and_1_out, full_alu_1_zero, control_logic_w_b_j_1_branch);
  Full_ALU full_alu_1 (
    .A(_16_bit_Reg_read_1_data), .B(multiplexer_2_out), .ALU_Control(ALUControl_operation),
    .Zero(full_alu_1_zero), .ALU_Out(full_alu_1_alu_out));
  ALU_Control ALUControl (
    .Function_code(ram_1_data[5:0]), .ALU_OP(control_logic_w_b_j_1_aluop), .Operation(ALUControl_operation));
  Multiplexer #(.width(16), .enable("false")) multiplexer_3 (
    .in0(adder_1_out), .in1(adder_2_out), .out(multiplexer_3_out), .sel(and_1_out));
  Multiplexer #(.width(16), .enable("false")) multiplexer_4 (
    .in0(multiplexer_3_out), .in1(ram_1_data[15:0]), .out(multiplexer_4_out), .sel(control_logic_w_b_j_1_jump));
  Multiplexer #(.width(16), .enable("false")) multiplexer_5 (
    .in0(full_alu_1_alu_out), .in1(ram_2_data), .out(multiplexer_5_out), .sel(control_logic_w_b_j_1_memtoreg));
  RAM #(.addrWidth(16), .dataWidth(16), .bus("separate")) ram_2 (
    .addr(full_alu_1_alu_out), .din(_16_bit_Reg_read_2_data), .data(ram_2_data),
    .str(control_logic_w_b_j_1_memwrite), .clk(clock), .ld(control_logic_w_b_j_1_memread));  // open: sel, clr

  // Notes on the sheet:
  //   Instruction Memory
  //   op
  //   src2
  //   WE
  //   Control Logic
  //   dest
  //   src1
  //   immed data
  //   RegDest
  //   Function code
  //   ALUSrc
  //   For Branch
  //   Zero
  //   Full ALU
  //   ALUOP
  //   Branch
  //   MemToReg
  //   MemWrite
  //   For jump
  //   MemRead
  //   Data Memory
endmodule

module Full_ALU_w__slt (
  input  [15:0] A,
  input  [15:0] B,
  input  [2:0] ALU_Control,
  output Zero,
  output [15:0] ALU_Out
);

  wire and_1_out, or_2_out;
  wire [0:0] comparator_1_lt;
  wire [15:0] adder_1_out, and_2_out, multiplexer_1_out, not_1_out, or_1_out;

  Multiplexer #(.width(16), .enable("false")) multiplexer_1 (
    .in0(B), .in1(not_1_out), .out(multiplexer_1_out), .sel(and_1_out));
  assign not_1_out = ~B;  // NOT_Gate not_1, 16 bits wide
  and and_1 (and_1_out, ALU_Control[1], ALU_Control[2]);
  assign and_2_out = A & multiplexer_1_out;  // AND_Gate and_2, 16 bits wide
  assign or_1_out = A | multiplexer_1_out;  // OR_Gate or_1, 16 bits wide
  Adder #(.width(16)) adder_1 (.a(A), .b(multiplexer_1_out), .out(adder_1_out), .cin(and_1_out));  // open: cout
  Comparator #(.width(16)) comparator_1 (.a(A), .b(B), .lt(comparator_1_lt[0]));  // open: gt, eq
  Multiplexer #(.select(3), .width(16), .enable("false")) multiplexer_2 (
    .in0(and_2_out), .in1(or_1_out), .in2(adder_1_out), .in6(adder_1_out),
    .in7({{15{1'b0}}, comparator_1_lt[0]}), .out(ALU_Out), .sel(ALU_Control));  // open: in3, in4, in5
  or or_2 (or_2_out, ALU_Out[0], ALU_Out[1], ALU_Out[2], ALU_Out[3], ALU_Out[4], ALU_Out[5], ALU_Out[6], ALU_Out[7], ALU_Out[8], ALU_Out[9], ALU_Out[10], ALU_Out[11], ALU_Out[12], ALU_Out[13], ALU_Out[14], ALU_Out[15]);
  not not_2 (Zero, or_2_out);

  // Notes on the sheet:
  //   000 - AND
  //   001 - OR
  //   010 - ADD
  //   110 - SUB
  //   111 - SLT
  //   sub not B
  //   sub cin
  //   sub
endmodule

module _16_bit_CPU_w__b__j__slt (
  input  clock
);

  wire and_1_out, control_logic_w_b_j_1_alusrc, control_logic_w_b_j_1_branch, control_logic_w_b_j_1_jump,
       control_logic_w_b_j_1_memread, control_logic_w_b_j_1_memtoreg, control_logic_w_b_j_1_memwrite,
       control_logic_w_b_j_1_regdest, control_logic_w_b_j_1_regwrite, full_alu_w_slt_1_zero;
  wire [1:0] control_logic_w_b_j_1_aluop;
  wire [2:0] ALUControl_operation, multiplexer_1_out;
  wire [15:0] _16_bit_Reg_read_1_data, _16_bit_Reg_read_2_data, adder_1_out, adder_2_out,
       full_alu_w_slt_1_alu_out, multiplexer_2_out, multiplexer_3_out, multiplexer_4_out, multiplexer_5_out,
       PC_q, ram_2_data;
  wire [27:0] ram_1_data;

  Register #(.width(16)) PC (.D(multiplexer_4_out), .Q(PC_q), .clk(clock));  // open: en, clr
  Adder #(.width(16)) adder_1 (.a(16'h1), .b(PC_q), .out(adder_1_out));  // open: cin, cout
  RAM #(.addrWidth(16), .dataWidth(28)) ram_1 (.addr(PC_q), .data(ram_1_data), .clk(clock));  // open: sel, ld, clr
  Control_Logic_w__b__j control_logic_w_b_j_1 (
    .in_1(ram_1_data[27:22]), .RegDest(control_logic_w_b_j_1_regdest), .ALUSrc(control_logic_w_b_j_1_alusrc),
    .MemToReg(control_logic_w_b_j_1_memtoreg), .RegWrite(control_logic_w_b_j_1_regwrite),
    .MemRead(control_logic_w_b_j_1_memread), .MemWrite(control_logic_w_b_j_1_memwrite),
    .Branch(control_logic_w_b_j_1_branch), .ALUOP(control_logic_w_b_j_1_aluop),
    .Jump(control_logic_w_b_j_1_jump));
  Multiplexer #(.width(3), .enable("false")) multiplexer_1 (
    .in0(ram_1_data[21:19]), .in1(ram_1_data[15:13]), .out(multiplexer_1_out),
    .sel(control_logic_w_b_j_1_regdest));
  _8x16_bit_Register_File _16_bit_Reg (
    .Data_In(multiplexer_5_out), .Write_Enable(control_logic_w_b_j_1_regwrite), .Clock(clock),
    .Write_Addr(ram_1_data[21:19]), .Read_Addr_1(ram_1_data[18:16]), .Read_Addr_2(multiplexer_1_out),
    .Read_1_Data(_16_bit_Reg_read_1_data), .Read_2_Data(_16_bit_Reg_read_2_data));
  Adder #(.width(16)) adder_2 (.a(adder_1_out), .b(ram_1_data[15:0]), .out(adder_2_out));  // open: cin, cout
  Multiplexer #(.width(16), .enable("false")) multiplexer_2 (
    .in0(_16_bit_Reg_read_2_data), .in1(ram_1_data[15:0]), .out(multiplexer_2_out),
    .sel(control_logic_w_b_j_1_alusrc));
  and and_1 (and_1_out, full_alu_w_slt_1_zero, control_logic_w_b_j_1_branch);
  Full_ALU_w__slt full_alu_w_slt_1 (
    .A(_16_bit_Reg_read_1_data), .B(multiplexer_2_out), .ALU_Control(ALUControl_operation),
    .Zero(full_alu_w_slt_1_zero), .ALU_Out(full_alu_w_slt_1_alu_out));
  ALU_Control ALUControl (
    .Function_code(ram_1_data[5:0]), .ALU_OP(control_logic_w_b_j_1_aluop), .Operation(ALUControl_operation));
  Multiplexer #(.width(16), .enable("false")) multiplexer_3 (
    .in0(adder_1_out), .in1(adder_2_out), .out(multiplexer_3_out), .sel(and_1_out));
  Multiplexer #(.width(16), .enable("false")) multiplexer_4 (
    .in0(multiplexer_3_out), .in1(ram_1_data[15:0]), .out(multiplexer_4_out), .sel(control_logic_w_b_j_1_jump));
  Multiplexer #(.width(16), .enable("false")) multiplexer_5 (
    .in0(full_alu_w_slt_1_alu_out), .in1(ram_2_data), .out(multiplexer_5_out),
    .sel(control_logic_w_b_j_1_memtoreg));
  RAM #(.addrWidth(16), .dataWidth(16), .bus("separate")) ram_2 (
    .addr(full_alu_w_slt_1_alu_out), .din(_16_bit_Reg_read_2_data), .data(ram_2_data),
    .str(control_logic_w_b_j_1_memwrite), .clk(clock), .ld(control_logic_w_b_j_1_memread));  // open: sel, clr

  // Notes on the sheet:
  //   Instruction Memory
  //   op
  //   src2
  //   WE
  //   Control Logic
  //   dest
  //   src1
  //   immed data
  //   RegDest
  //   Function code
  //   ALUSrc
  //   For Branch
  //   Zero
  //   Full ALU
  //   ALUOP
  //   Branch
  //   MemToReg
  //   MemWrite
  //   For jump
  //   MemRead
  //   Data Memory
endmodule
